// Logisim project reg-v2.circ as structural Verilog: 2 circuits, main circuit Four_Input_Register
module Sub_Register (
  input  clock_1,
  input  [7:0] in_1,
  output [7:0] out_1
);
endmodule

module Four_Input_Register (
  input  [7:0] data_in,
  output [7:0] data_out
);

  Adder adder_1 ();  // open: a, b, out, cin, cout
  Clock clock_2 ();  // open: out
  Sub_Register sub_register_1 ();  // open: clock_1, in_1, out_1

  // Notes on the sheet:
  //   8-bit constant 0
  //   8-bbit constant 1
endmodule
